# Fritzing sketch seriesLED (saved by Fritzing 0.9.4)
breadboards: 1

parts:
  Part1 = Arduino Nano (Rev3.0)
  R1 = Resistor [tolerance=±5% resistance=220 package=THT]
  S1 = Pushbutton [package="[THT]"]
  LED2 = LED - 5mm [color="Red (633nm)" package="5 mm [THT]"]
  LED3 = LED - 5mm [color="Red (633nm)" package="5 mm [THT]"]

nets:
  N1: Part1.GND, LED3.cathode
  N2: Part1.5V, R1.Pin_1
  N3: R1.Pin_0, S1.Pin_3, S1.Pin_4, LED2.anode
  N4: S1.Pin_1, S1.Pin_2
  N5: LED2.cathode, LED3.anode
