# Fritzing sketch piezo (saved by Fritzing 0.9.4)
breadboards: 1

parts:
  LED2 = RGB LED (com. cathode, rgb) [package="5 mm [THT]"]
  Part1 = Arduino Nano (Rev3.0)
  R3 = Resistor [tolerance=±5% resistance=220 package=THT]
  R4 = Resistor [tolerance=±5% resistance=220 package=THT]
  R5 = Resistor [tolerance=±5% resistance=220 package=THT]

nets:
  N1: LED2.red_anode, Part1.GND
  N2: LED2.common_cathode, R3.Pin_1
  N3: LED2.green_anode, R4.Pin_1
  N4: LED2.blue_anode, R5.Pin_1
  N5: Part1.D3, R3.Pin_0
  N6: Part1.D5, R4.Pin_0
  N7: Part1.D7, R5.Pin_0
